# Fritzing sketch FRITZINGSCHEMATICOriginal (saved by Fritzing 0.9.3b)

parts:
  U1 = ESP8266 NodeMCU LoLin module
  U3 = BATTERY-2 [package=battery-aa]
  J2 = Basic Servo
  U4 = LM2596 step down module
  J1 = Basic Servo
  HC-SR04_Sensor_1 = HC-SR04 Ultrasonic Distance Sensor

nets:
  N1: U1.D1, J1.pulse
  N2: U1.D2, J2.pulse
  GND: U1.GND, U3.-1, J2.gnd
  N3: U1.D5, HC-SR04_Sensor_1.ECHO
  N4: U1.D6, HC-SR04_Sensor_1.TRIG
  N5: U3.+1, U4.IN+
  N6: U4.IN-, U4.OUT-
  VCC: J1.vcc, HC-SR04_Sensor_1.VCC

custom parts:
  ESP8266 NodeMCU LoLin module: ESP8266 based NodeMCU
  LM2596 step down module: LM2596 DC-DC step down power supply module 3 A.
